# Fritzing sketch garage (saved by Fritzing 0.9.2b)
perfboards: 1

parts:
  J1 = Screw terminal - 2 pins [package=THT]
  Q1 = NPN-Transistor [package="TO92 [THT]"]
  D1 = Rectifier Diode [part_number=1N4001 package="300 mil [THT]"]
  J2 = Screw terminal - 2 pins [package=THT]
  S1 = Pushbutton [package="[THT]"]
  R1 = Resistor [tolerance=±5% resistance=220 package=THT]
  Part2 = HUZZAH ESP8266 Breakout
  DIP-Relay1 = DIP-Relay-D31A [part_number=D31A*]
  R2 = Resistor [tolerance=±5% resistance=220 package="0402 [SMD]"]

nets:
  N1: J1.pin1, Q1.E, Part2.GND
  N2: J1.pin2, D1.cathode, DIP-Relay1.B1_Switch_Terminal_B
  N3: Q1.B, R2.Pin_0
  N4: Q1.C, D1.anode, DIP-Relay1.B2_Switch_Terminal_B
  N5: J2.pin1, DIP-Relay1.COIL1_+
  N6: J2.pin2, DIP-Relay1.A1_Switch_Terminal_A
  N7: S1.Pin_1, S1.Pin_2, Part2.3.3V
  N8: S1.Pin_3, S1.Pin_4, R1.Pin_1
  N9: R1.Pin_0, Part2.GPIO16
  N10: Part2.GPIO12, R2.Pin_1

custom parts:
  HUZZAH ESP8266 Breakout: The ESP8266 processor from Espressif is an 80 MHz microcontroller with a full WiFi front-end (both as client and access point) and TCP/IP stack with DNS support as well.
